# Fritzing sketch power_connections (saved by Fritzing 0.8.7b)
breadboards: 1

parts:
  S1 = Toggle Switch [package=THT]
  Power_plug1 = Power plug
  Part1 = Arduino Nano (Rev3.0)
  R1 = Resistor [tolerance=±5% resistance=470 package=THT]
  LED1 = LED - 5mm [color="Red (633nm)" package="5 mm [THT]"]

nets:
  N1: S1.L1, Power_plug1.VCC
  N2: S1.COM, Part1.VIN
  GND: Power_plug1.GND, Part1.GND, LED1.cathode
  N3: Part1.5V, R1.Pin_0
